# Fritzing sketch Schema (saved by Fritzing 0.9.0b)
breadboards: 1

parts:
  Parte1 = Arduino Mega 2560 (Rev3)
  IC1 = ULN2803A [package=THT]
  12V_External_Source = Power plug
  12V = LEDs [package=fkit-led-1206]
  12V_2 = LEDs [package=fkit-led-1206]
  12V_3 = LEDs [package=fkit-led-1206]
  12V_4 = LEDs [package=fkit-led-1206]
  12V_5 = LEDs [package=fkit-led-1206]
  12V_6 = LEDs [package=fkit-led-1206]
  Parte2 = Arduino Board Ethernet  # not connected

nets:
  N1: Parte1.D22, IC1.In_1
  N2: Parte1.D23, IC1.In_2
  N3: Parte1.D24, IC1.In_3
  N4: Parte1.D25, IC1.In_4
  N5: Parte1.D26, IC1.In_5
  N6: Parte1.D27, IC1.In_6
  GND: IC1.0V, 12V_External_Source.GND
  N7: IC1.Out_6, 12V_5.C
  N8: IC1.Out_5, 12V_6.C
  N9: IC1.Out_4, 12V_4.C
  N10: IC1.Out_3, 12V_3.C
  N11: IC1.Out_2, 12V_2.C
  N12: IC1.Out_1, 12V.C
  N13: 12V_External_Source.VCC, 12V.A, 12V_2.A, 12V_3.A, 12V_4.A, 12V_5.A, 12V_6.A

notes:
  12V external source
